// Digital circuit Airport terminal tram.dig as structural Verilog
module Airport_terminal_tram (
  input  clk,
  input  reset,
  input  c1,
  input  c2
);

  wire a0, and_1_out, and_2_out, and_3_out, and_4_out, and_5_out, and_6_out, and_7_out, and_8_out, and_9_out,
       and_10_out, and_11_out, and_12_out, and_13_out, and_14_out, and_15_out, and_16_out, and_17_out, green,
       invert, nc1, nc2, not_1_out, nq0, nq1, nq2, or_4_out, or_5_out, or_6_out, q0, q1, q2;
  wire [3:0] alu_1_y, four_bit_reg_1_q;

  and and_1 (and_1_out, nq2, q0);
  and and_2 (and_2_out, q2, nq0);
  and and_3 (and_3_out, q2, q0);
  and and_4 (and_4_out, q2, q0);
  and and_5 (and_5_out, nq2, nq1, nq0);
  or or_1 (a0, q1, and_1_out, and_2_out);
  or or_2 (invert, q1, and_3_out);
  or or_3 (green, and_4_out, and_5_out);
  alu alu_1 (
    .a({3'b000, a0}), .b(four_bit_reg_1_q), .invert(invert), .arith(1'b1), .pass(1'b0), .cin(1'b0),
    .y(alu_1_y));  // open: cout, overfl
  four_bit_reg four_bit_reg_1 (.d(alu_1_y), .enable(1'b1), .reset(reset), .clk(clk), .q(four_bit_reg_1_q));
  not not_1 (not_1_out, green);
  LED led_1 (.in(not_1_out));
  LED led_2 (.in(green));
  not not_2 (nc1, c1);
  not not_3 (nc2, c2);
  Seven_Seg_Hex seven_seg_hex_1 (.d(four_bit_reg_1_q), .dp(1'b0));
  and and_6 (and_6_out, nc1, nc2, q1);
  and and_7 (and_7_out, c2, nq1, nq0);
  and and_8 (and_8_out, q1, nq0, c1);
  and and_9 (and_9_out, q1, nc1, nc2);
  and and_10 (and_10_out, nc1, nc2, q1);
  and and_11 (and_11_out, nq2, c1, nc2, nq1);
  and and_12 (and_12_out, nq2, c2, nq1, q0);
  and and_13 (and_13_out, q2, nc1, nc2, q0);
  and and_14 (and_14_out, q2, c1, c2, q0);
  and and_15 (and_15_out, c1, q1);
  and and_16 (and_16_out, c1, nc2, nq0);
  and and_17 (and_17_out, q2, c1, nc2);
  or or_4 (or_4_out, and_10_out, and_11_out, and_12_out, and_13_out, and_14_out);
  or or_5 (or_5_out, and_15_out, and_16_out, and_17_out);
  or or_6 (or_6_out, and_6_out, and_7_out, and_8_out, and_9_out);
  D_FF_AS d_ff_as_1 (.Set(1'b0), .D(or_5_out), .C(clk), .Clr(reset), .Q(q1), .nQ(nq1));
  D_FF_AS d_ff_as_2 (.Set(1'b0), .D(or_4_out), .C(clk), .Clr(reset), .Q(q2), .nQ(nq2));
  D_FF_AS d_ff_as_3 (.Set(1'b0), .D(or_6_out), .C(clk), .Clr(reset), .Q(q0), .nQ(nq0));
endmodule
