// Digital circuit alu.dig as structural Verilog
module alu (
  input  [3:0] a,
  input  [3:0] b,
  input  invert,
  input  arith,
  input  pass,
  input  cin,
  output [3:0] y,
  output cout,
  output overfl
);

  wire not_neg_1_p4;

  // not_neg not_neg_1: pin names not known; wires that end beside it: a, invert, arith, not_neg_1_p4
  // and_add and_add_1: pin names not known; wires that end beside it: not_neg_1_p4, b, arith, cin, pass, y, cout, overfl
endmodule
